# Fritzing sketch Controller_PCB_v3 (saved by Fritzing 0.9.2b)
circuit board: 6.88566cm x 5.36311cm
breadboards: 1

parts:
  CD4021BE = IC, DIP package, 16 pins [chip_label=CD4021BE]
  R1 = Resistor [tolerance=±5% resistance=1k package=THT]
  C1 = Ceramic Capacitor [capacitance=100nF package="100 mil [THT, multilayer]"]
  R2 = Resistor [tolerance=±5% resistance=1k package=THT]
  R3 = Resistor [tolerance=±5% resistance=1k package=THT]
  R4 = Resistor [tolerance=±5% resistance=1k package=THT]
  R5 = Resistor [tolerance=±5% resistance=1k package=THT]
  R6 = Resistor [tolerance=±5% resistance=1k package=THT]
  R7 = Resistor [tolerance=±5% resistance=1k package=THT]
  R8 = Resistor [tolerance=±5% resistance=1k package=THT]
  R9 = Resistor [tolerance=±5% resistance=10k package=THT]
  R10 = Resistor [tolerance=±5% resistance=10k package=THT]
  R11 = Resistor [tolerance=±5% resistance=10k package=THT]
  R12 = Resistor [tolerance=±5% resistance=10k package=THT]
  B1 = female pin header, 8 pins [form="♀ (female)"]
  B2 = female pin header, 8 pins [form="♀ (female)"]
  L_KB = female pin header, 4 pins [form="♀ (female)"]
  R_KB = female pin header, 4 pins [form="♀ (female)"]
  SDVX_CTRL = Arduino Leonardo (Rev3b)

nets:
  N1: CD4021BE.pin1, R6.Pin_0, B2.pin8
  N2: CD4021BE.pin3, SDVX_CTRL.D9_PWM/A9
  N3: CD4021BE.pin4, R4.Pin_0, B2.pin4
  N4: CD4021BE.pin5, R3.Pin_0, B2.pin3
  N5: CD4021BE.pin6, R2.Pin_0, B2.pin2
  N6: CD4021BE.pin7, R1.Pin_0, B2.pin1
  N7: CD4021BE.pin8, R1.Pin_1, C1.1, R2.Pin_1, R3.Pin_1, R4.Pin_1, R5.Pin_1, R6.Pin_1, R7.Pin_1, R8.Pin_1, L_KB.pin4, R_KB.pin4, SDVX_CTRL.GND
  N8: CD4021BE.pin9, SDVX_CTRL.D8/A8
  N9: CD4021BE.pin10, SDVX_CTRL.D7
  N10: CD4021BE.pin13, R5.Pin_0, B2.pin5
  N11: CD4021BE.pin14, R8.Pin_0, B2.pin6
  N12: CD4021BE.pin15, R7.Pin_0, B2.pin7
  N13: CD4021BE.pin16, C1.0, R9.Pin_1, R10.Pin_1, R11.Pin_1, R12.Pin_1, B1.pin1, B1.pin2, B1.pin3, B1.pin4, B1.pin5, B1.pin6, B1.pin7, B1.pin8, L_KB.pin1, R_KB.pin1, SDVX_CTRL.5V
  N14: R9.Pin_0, L_KB.pin2, SDVX_CTRL.D2/SDA
  N15: R10.Pin_0, L_KB.pin3, SDVX_CTRL.D4/A6
  N16: R11.Pin_0, R_KB.pin2, SDVX_CTRL.D3_PWM/SCL
  N17: R12.Pin_0, R_KB.pin3, SDVX_CTRL.D5_PWM

notes:
  BUTTONS
